// Logisim project 4x8multiplier.circ as structural Verilog: 6 circuits, main circuit main
module main (
  input  in_1,
  input  in_2,
  input  in_3,
  input  b0,
  input  a3,
  input  a2,
  input  a1,
  input  a0,
  input  b3,
  input  b2,
  input  b1,
  input  in_12,
  input  a7,
  input  a6,
  input  a5,
  input  a4,
  output out_17,
  output out_18,
  output out_19,
  output out_20,
  output out_21,
  output out_22,
  output out_23,
  output out_24,
  output out_25,
  output out_26,
  output out_27,
  output out_28
);

  wire l_4x4multiplier_616cc757_1_out_13, l_4x4multiplier_616cc757_1_out_14,
       l_4x4multiplier_616cc757_1_out_15, l_4x4multiplier_616cc757_1_out_16,
       l_4x4multiplier_616cc757_1_out_17, l_4x4multiplier_616cc757_1_out_18,
       l_4x4multiplier_616cc757_1_out_19, l_4x4multiplier_616cc757_1_out_20,
       l_4x4multiplier_616cc757_2_out_15, l_4x4multiplier_616cc757_2_out_16,
       l_4x4multiplier_616cc757_2_out_17, l_4x4multiplier_616cc757_2_out_19;

  L_4x4multiplier_616cc757 l_4x4multiplier_616cc757_1 (
    .B3(b3), .B2(b2), .B1(b1), .B0(in_12), .A3(a7), .L_2_491f351e(1'b0), .A2(a6), .A1(a5), .A0(a4),
    .out_15(l_4x4multiplier_616cc757_1_out_15), .out_16(l_4x4multiplier_616cc757_1_out_16),
    .out_17(l_4x4multiplier_616cc757_1_out_17), .out_19(l_4x4multiplier_616cc757_1_out_19),
    .out_13(l_4x4multiplier_616cc757_1_out_13), .out_14(l_4x4multiplier_616cc757_1_out_14),
    .out_18(l_4x4multiplier_616cc757_1_out_18), .out_20(l_4x4multiplier_616cc757_1_out_20),
    .L_3_6e08a9d7(1'b0), .L_1_083988bd(1'b0), .L_4_8c3c58d8(1'b0));
  L_8_bit_adder_92b21574 l_8_bit_adder_92b21574_1 (
    .a0(l_4x4multiplier_616cc757_2_out_19), .b0(l_4x4multiplier_616cc757_1_out_20),
    .in_4(l_4x4multiplier_616cc757_2_out_17), .b1(l_4x4multiplier_616cc757_1_out_18),
    .in_6(l_4x4multiplier_616cc757_2_out_16), .in_7(l_4x4multiplier_616cc757_1_out_14),
    .in_8(l_4x4multiplier_616cc757_2_out_15), .a3(l_4x4multiplier_616cc757_1_out_13), .in_10(1'b0),
    .in_11(l_4x4multiplier_616cc757_1_out_19), .a1(1'b0), .in_13(l_4x4multiplier_616cc757_1_out_17),
    .a2(1'b0), .b2(l_4x4multiplier_616cc757_1_out_16), .b3(1'b0), .in_17(l_4x4multiplier_616cc757_1_out_15),
    .in(1'b0), .out_18(out_24), .out_19(out_23), .out_20(out_22), .out_21(out_21), .out_22(out_20),
    .out_23(out_19), .out_24(out_18), .out_25(out_17));  // open: out_26
  L_4x4multiplier_616cc757 l_4x4multiplier_616cc757_2 (
    .B3(in_1), .B2(in_2), .B1(in_3), .B0(b0), .A3(a3), .L_2_491f351e(1'b0), .A2(a2), .A1(a1), .A0(a0),
    .out_15(l_4x4multiplier_616cc757_2_out_15), .out_16(l_4x4multiplier_616cc757_2_out_16),
    .out_17(l_4x4multiplier_616cc757_2_out_17), .out_19(l_4x4multiplier_616cc757_2_out_19), .out_13(out_28),
    .out_14(out_25), .out_18(out_26), .out_20(out_27), .L_3_6e08a9d7(1'b0), .L_1_083988bd(1'b0),
    .L_4_8c3c58d8(1'b0));
endmodule

module full_adder_dfd2a586 (
  input  in_1,
  input  in_2,
  input  in_3,
  output out_4,
  output out_5
);

  Adder #(.width(1)) adder_1 (.a(in_2), .b(in_3), .out(out_4), .cin(in_1), .cout(out_5));
endmodule

module L_4x4multiplier_616cc757 (
  input  B3,
  input  B2,
  input  B1,
  input  B0,
  input  A3,
  input  A2,
  input  A1,
  input  A0,
  input  L_2_491f351e,
  input  L_3_6e08a9d7,
  input  L_1_083988bd,
  input  L_4_8c3c58d8,
  output out_13,
  output out_14,
  output out_15,
  output out_16,
  output out_17,
  output out_18,
  output out_19,
  output out_20
);

  wire and_1_out, and_2_out, and_3_out, and_4_out, and_5_out, and_6_out, and_7_out, and_8_out, and_9_out,
       and_10_out, and_11_out, and_12_out, and_13_out, and_14_out, and_15_out, full_adder_dfd2a586_2_out_4,
       full_adder_dfd2a586_2_out_5, full_adder_dfd2a586_3_out_4, full_adder_dfd2a586_3_out_5,
       full_adder_dfd2a586_4_out_5, full_adder_dfd2a586_5_out_4, full_adder_dfd2a586_5_out_5,
       full_adder_dfd2a586_6_out_4, full_adder_dfd2a586_6_out_5, full_adder_dfd2a586_7_out_4,
       full_adder_dfd2a586_7_out_5, full_adder_dfd2a586_8_out_5, full_adder_dfd2a586_9_out_4,
       full_adder_dfd2a586_9_out_5, full_adder_dfd2a586_10_out_5, full_adder_dfd2a586_11_out_5,
       full_adder_dfd2a586_12_out_5;

  and and_1 (and_1_out, A3, B3);
  full_adder_dfd2a586 full_adder_dfd2a586_1 (
    .in_2(and_1_out), .in_3(full_adder_dfd2a586_2_out_5), .in_1(full_adder_dfd2a586_4_out_5), .out_5(out_15),
    .out_4(out_16));
  and and_2 (and_2_out, A3, B2);
  full_adder_dfd2a586 full_adder_dfd2a586_2 (
    .in_2(and_2_out), .in_3(full_adder_dfd2a586_3_out_5), .in_1(full_adder_dfd2a586_6_out_5),
    .out_5(full_adder_dfd2a586_2_out_5), .out_4(full_adder_dfd2a586_2_out_4));
  and and_3 (and_3_out, A3, B0);
  and and_4 (and_4_out, B1, A3);
  full_adder_dfd2a586 full_adder_dfd2a586_3 (
    .in_2(L_2_491f351e), .in_3(and_4_out), .in_1(full_adder_dfd2a586_5_out_5),
    .out_5(full_adder_dfd2a586_3_out_5), .out_4(full_adder_dfd2a586_3_out_4));
  and and_5 (and_5_out, A2, B3);
  full_adder_dfd2a586 full_adder_dfd2a586_4 (
    .in_2(and_5_out), .in_3(full_adder_dfd2a586_2_out_4), .in_1(full_adder_dfd2a586_8_out_5),
    .out_5(full_adder_dfd2a586_4_out_5), .out_4(out_17));
  and and_6 (and_6_out, B1, A2);
  full_adder_dfd2a586 full_adder_dfd2a586_5 (
    .in_2(and_6_out), .in_3(and_3_out), .in_1(full_adder_dfd2a586_9_out_5),
    .out_5(full_adder_dfd2a586_5_out_5), .out_4(full_adder_dfd2a586_5_out_4));
  and and_7 (and_7_out, A2, B2);
  full_adder_dfd2a586 full_adder_dfd2a586_6 (
    .in_2(and_7_out), .in_3(full_adder_dfd2a586_3_out_4), .in_1(full_adder_dfd2a586_7_out_5),
    .out_5(full_adder_dfd2a586_6_out_5), .out_4(full_adder_dfd2a586_6_out_4));
  and and_8 (and_8_out, A2, B0);
  and and_9 (and_9_out, B1, A1);
  and and_10 (and_10_out, A1, B2);
  full_adder_dfd2a586 full_adder_dfd2a586_7 (
    .in_2(and_10_out), .in_3(full_adder_dfd2a586_5_out_4), .in_1(full_adder_dfd2a586_10_out_5),
    .out_5(full_adder_dfd2a586_7_out_5), .out_4(full_adder_dfd2a586_7_out_4));
  and and_11 (and_11_out, A1, B3);
  full_adder_dfd2a586 full_adder_dfd2a586_8 (
    .in_2(and_11_out), .in_3(full_adder_dfd2a586_6_out_4), .in_1(full_adder_dfd2a586_11_out_5),
    .out_5(full_adder_dfd2a586_8_out_5), .out_4(out_19));
  and and_12 (and_12_out, A1, B0);
  full_adder_dfd2a586 full_adder_dfd2a586_9 (
    .in_2(and_9_out), .in_3(and_8_out), .in_1(full_adder_dfd2a586_12_out_5),
    .out_5(full_adder_dfd2a586_9_out_5), .out_4(full_adder_dfd2a586_9_out_4));
  and and_13 (and_13_out, A0, B2);
  full_adder_dfd2a586 full_adder_dfd2a586_10 (
    .in_2(and_13_out), .in_3(full_adder_dfd2a586_9_out_4), .in_1(L_1_083988bd),
    .out_5(full_adder_dfd2a586_10_out_5), .out_4(out_14));
  and and_14 (and_14_out, A0, B3);
  full_adder_dfd2a586 full_adder_dfd2a586_11 (
    .in_2(and_14_out), .in_3(full_adder_dfd2a586_7_out_4), .in_1(L_4_8c3c58d8),
    .out_5(full_adder_dfd2a586_11_out_5), .out_4(out_13));
  and and_15 (and_15_out, B1, A0);
  full_adder_dfd2a586 full_adder_dfd2a586_12 (
    .in_2(and_15_out), .in_3(and_12_out), .in_1(L_3_6e08a9d7), .out_5(full_adder_dfd2a586_12_out_5),
    .out_4(out_18));
  and and_16 (out_20, B0, A0);
endmodule

module L_4_bit_adder_2a8fa939 (
  input  in,
  input  a0,
  input  b0,
  input  a1,
  input  b1,
  input  a2,
  input  b2,
  input  a3,
  input  b3,
  output o0,
  output o1,
  output o2,
  output o3,
  output out
);

  wire adder_1_cout, adder_2_cout, adder_3_cout;

  Adder #(.width(1)) adder_1 (.a(a0), .b(b0), .out(o0), .cin(in), .cout(adder_1_cout));
  Adder #(.width(1)) adder_2 (.a(a1), .b(b1), .out(o1), .cin(adder_1_cout), .cout(adder_2_cout));
  Adder #(.width(1)) adder_3 (.a(a2), .b(b2), .out(o2), .cin(adder_2_cout), .cout(adder_3_cout));
  Adder #(.width(1)) adder_4 (.a(a3), .b(b3), .out(o3), .cin(adder_3_cout), .cout(out));
endmodule

module L_8_bit_adder_92b21574 (
  input  in,
  input  a0,
  input  b0,
  input  in_4,
  input  b1,
  input  in_6,
  input  in_7,
  input  in_8,
  input  a3,
  input  in_10,
  input  in_11,
  input  a1,
  input  in_13,
  input  a2,
  input  b2,
  input  b3,
  input  in_17,
  output out_18,
  output out_19,
  output out_20,
  output out_21,
  output out_22,
  output out_23,
  output out_24,
  output out_25,
  output out_26
);

  wire l_4_bit_adder_2a8fa939_1_out;

  L_4_bit_adder_2a8fa939 l_4_bit_adder_2a8fa939_1 (
    .a0(a0), .b0(b0), .a1(in_4), .b1(b1), .a2(in_6), .b2(in_7), .a3(a3), .b3(in_8), .in(in),
    .out(l_4_bit_adder_2a8fa939_1_out), .o0(out_18), .o1(out_19), .o2(out_20), .o3(out_21));
  L_4_bit_adder_2a8fa939 l_4_bit_adder_2a8fa939_2 (
    .a0(in_10), .b0(in_11), .a1(a1), .b1(in_13), .a2(a2), .b2(b2), .a3(in_17), .b3(b3),
    .in(l_4_bit_adder_2a8fa939_1_out), .out(out_26), .o0(out_22), .o1(out_23), .o2(out_24), .o3(out_25));
endmodule

module ful_adder_ff0069c6 (
  input  in_1,
  input  in_2,
  input  in_3,
  output out_4,
  output out_5
);

  Adder #(.width(1)) adder_1 (.a(in_2), .b(in_3), .out(out_4), .cin(in_1), .cout(out_5));
endmodule
