// Logisim project ParkingCalculator.circ as structural Verilog: 2 circuits, main circuit main
module main (
  input  _0,
  input  in_2,
  input  in_3,
  input  in_4,
  input  in_5,
  input  in_6,
  input  in_7,
  input  in_8,
  input  in_9,
  input  _9,
  input  in_11,
  input  in_12,
  input  in_13,
  input  in_14,
  input  in_15,
  input  in_16,
  input  in_17,
  input  in_18,
  input  in_19,
  input  in_20,
  input  in_21,
  input  in_22,
  input  in_23,
  input  in_24,
  input  in_25,
  input  in_26,
  input  [7:0] in_27,
  input  [7:0] in_28,
  input  [7:0] in_29,
  input  [7:0] in_30,
  input  [7:0] in_31,
  input  [7:0] in_32,
  input  [3:0] in_33,
  input  [3:0] in_34,
  input  [3:0] in_35,
  input  [3:0] in_36,
  input  in_37,
  input  in_38,
  input  in_39,
  input  in_40,
  input  in_41,
  input  in_42,
  input  in_43,
  input  in_44,
  input  in_45,
  input  w,
  input  x,
  input  y,
  input  in_49,
  input  in_50,
  input  in_51,
  input  in_52,
  output out_53,
  output out_54,
  output out_55,
  output out_56,
  output out_57,
  output out_58,
  output out_59,
  output out_60,
  output out_61,
  output out_62,
  output out_63,
  output LSB,
  output out_65,
  output [7:0] out_66,
  output [7:0] out_67,
  output out_68,
  output [7:0] out_69,
  output [7:0] out_70,
  output [7:0] out_71,
  output [7:0] out_72,
  output out_73,
  output out_74,
  output out_75,
  output out_76,
  output out_77,
  output out_78,
  output out_79,
  output out_80,
  output out_81,
  output out_82,
  output out_83,
  output out_84,
  output out_85,
  output out_86,
  output out_87,
  output out_88,
  output out_89,
  output out_90,
  output out_91,
  output out_92,
  output out_93,
  output out_94,
  output out_95,
  output out_96,
  output out_97,
  output out_98,
  output out_99,
  output out_100,
  output out_101,
  output out_102,
  output out_103,
  output out_104,
  output out_105,
  output out_106,
  output out_107,
  output out_108,
  output out_109,
  output out_110,
  output out_111,
  output out_112
);

  wire A_out, and_1_out, and_2_out, and_3_out, and_4_out, and_5_out, and_6_out, and_7_out, and_8_out,
       and_9_out, and_10_out, and_11_out, and_12_out, and_13_out, and_14_out, and_15_out, and_16_out, B_out,
       C_out, comparator_1_eq, comparator_1_lt, D_out, ful_adder_ff0069c6_2_out_4,
       ful_adder_ff0069c6_2_out_5, ful_adder_ff0069c6_3_out_5, ful_adder_ff0069c6_4_out_4,
       ful_adder_ff0069c6_4_out_5, ful_adder_ff0069c6_5_out_5, ful_adder_ff0069c6_6_out_4,
       ful_adder_ff0069c6_6_out_5, ful_adder_ff0069c6_7_out_4, ful_adder_ff0069c6_7_out_5,
       ful_adder_ff0069c6_8_out_4, ful_adder_ff0069c6_8_out_5, ful_adder_ff0069c6_9_out_5,
       ful_adder_ff0069c6_10_out_4, ful_adder_ff0069c6_10_out_5, ful_adder_ff0069c6_11_out_4,
       ful_adder_ff0069c6_11_out_5, ful_adder_ff0069c6_12_out_5, ful_adder_ff0069c6_13_out_4,
       ful_adder_ff0069c6_13_out_5, ful_adder_ff0069c6_14_out_4, ful_adder_ff0069c6_14_out_5,
       ful_adder_ff0069c6_15_out_4, ful_adder_ff0069c6_15_out_5, ful_adder_ff0069c6_16_out_4,
       ful_adder_ff0069c6_16_out_5, ful_adder_ff0069c6_17_out_5, ful_adder_ff0069c6_18_out_4,
       ful_adder_ff0069c6_18_out_5, ful_adder_ff0069c6_19_out_5, ful_adder_ff0069c6_20_out_5, not_1_out,
       not_2_out, not_3_out, not_4_out, not_5_out, not_6_out, not_7_out, not_8_out, not_9_out, not_10_out,
       not_11_out, not_12_out, not_13_out, not_14_out, not_15_out, not_16_out, or_4_out, undriven;
  wire [7:0] multiplier_1_out;

  or D (D_out, _9, in_9);
  or C (C_out, in_8, in_7, in_6, in_5);
  or B (B_out, in_8, in_7, in_4, in_3);
  or A (A_out, in_2, in_4, in_6, in_8, _9);
  ful_adder_ff0069c6 ful_adder_ff0069c6_1 (
    .in_2(in_25), .in_3(ful_adder_ff0069c6_2_out_5), .in_1(ful_adder_ff0069c6_3_out_5), .out_5(out_56),
    .out_4(out_57));
  and and_1 (and_1_out, 1'b1, D_out);
  ful_adder_ff0069c6 ful_adder_ff0069c6_2 (
    .in_2(and_1_out), .in_3(ful_adder_ff0069c6_4_out_5), .in_1(ful_adder_ff0069c6_8_out_5),
    .out_5(ful_adder_ff0069c6_2_out_5), .out_4(ful_adder_ff0069c6_2_out_4));
  ful_adder_ff0069c6 ful_adder_ff0069c6_3 (
    .in_2(in_25), .in_3(ful_adder_ff0069c6_2_out_4), .in_1(ful_adder_ff0069c6_5_out_5),
    .out_5(ful_adder_ff0069c6_3_out_5), .out_4(out_58));
  and and_2 (and_2_out, B_out, 1'b1);
  and and_3 (and_3_out, 1'b1, C_out);
  ful_adder_ff0069c6 ful_adder_ff0069c6_4 (
    .in_2(and_3_out), .in_3(ful_adder_ff0069c6_6_out_5), .in_1(ful_adder_ff0069c6_7_out_5),
    .out_5(ful_adder_ff0069c6_4_out_5), .out_4(ful_adder_ff0069c6_4_out_4));
  ful_adder_ff0069c6 ful_adder_ff0069c6_5 (
    .in_2(ful_adder_ff0069c6_8_out_4), .in_3(in_25), .in_1(ful_adder_ff0069c6_9_out_5),
    .out_5(ful_adder_ff0069c6_5_out_5), .out_4(out_59));
  and and_4 (and_4_out, 1'b1, A_out);
  ful_adder_ff0069c6 ful_adder_ff0069c6_6 (
    .in_2(in_21), .in_3(and_2_out), .in_1(ful_adder_ff0069c6_10_out_5), .out_5(ful_adder_ff0069c6_6_out_5),
    .out_4(ful_adder_ff0069c6_6_out_4));
  and and_5 (and_5_out, 1'b0, C_out);
  ful_adder_ff0069c6 ful_adder_ff0069c6_7 (
    .in_2(and_5_out), .in_3(ful_adder_ff0069c6_6_out_4), .in_1(ful_adder_ff0069c6_14_out_5),
    .out_5(ful_adder_ff0069c6_7_out_5), .out_4(ful_adder_ff0069c6_7_out_4));
  and and_6 (and_6_out, 1'b0, D_out);
  ful_adder_ff0069c6 ful_adder_ff0069c6_8 (
    .in_2(and_6_out), .in_3(ful_adder_ff0069c6_4_out_4), .in_1(ful_adder_ff0069c6_11_out_5),
    .out_5(ful_adder_ff0069c6_8_out_5), .out_4(ful_adder_ff0069c6_8_out_4));
  ful_adder_ff0069c6 ful_adder_ff0069c6_9 (
    .in_2(ful_adder_ff0069c6_11_out_4), .in_3(in_25), .in_1(ful_adder_ff0069c6_12_out_5),
    .out_5(ful_adder_ff0069c6_9_out_5), .out_4(out_60));
  and and_7 (and_7_out, 1'b0, A_out);
  and and_8 (and_8_out, B_out, 1'b0);
  ful_adder_ff0069c6 ful_adder_ff0069c6_10 (
    .in_2(and_8_out), .in_3(and_4_out), .in_1(ful_adder_ff0069c6_13_out_5),
    .out_5(ful_adder_ff0069c6_10_out_5), .out_4(ful_adder_ff0069c6_10_out_4));
  and and_9 (and_9_out, 1'b1, D_out);
  ful_adder_ff0069c6 ful_adder_ff0069c6_11 (
    .in_2(and_9_out), .in_3(ful_adder_ff0069c6_7_out_4), .in_1(ful_adder_ff0069c6_16_out_5),
    .out_5(ful_adder_ff0069c6_11_out_5), .out_4(ful_adder_ff0069c6_11_out_4));
  ful_adder_ff0069c6 ful_adder_ff0069c6_12 (
    .in_2(out_53), .in_3(ful_adder_ff0069c6_16_out_4), .in_1(ful_adder_ff0069c6_17_out_5),
    .out_5(ful_adder_ff0069c6_12_out_5), .out_4(out_61));
  and and_10 (and_10_out, B_out, 1'b1);
  ful_adder_ff0069c6 ful_adder_ff0069c6_13 (
    .in_2(and_10_out), .in_3(and_7_out), .in_1(ful_adder_ff0069c6_18_out_5),
    .out_5(ful_adder_ff0069c6_13_out_5), .out_4(ful_adder_ff0069c6_13_out_4));
  and and_11 (and_11_out, 1'b1, C_out);
  ful_adder_ff0069c6 ful_adder_ff0069c6_14 (
    .in_2(and_11_out), .in_3(ful_adder_ff0069c6_10_out_4), .in_1(ful_adder_ff0069c6_15_out_5),
    .out_5(ful_adder_ff0069c6_14_out_5), .out_4(ful_adder_ff0069c6_14_out_4));
  ful_adder_ff0069c6 ful_adder_ff0069c6_15 (
    .in_2(and_15_out), .in_3(ful_adder_ff0069c6_13_out_4), .in_1(in_23), .out_5(ful_adder_ff0069c6_15_out_5),
    .out_4(ful_adder_ff0069c6_15_out_4));
  and and_12 (and_12_out, 1'b0, D_out);
  ful_adder_ff0069c6 ful_adder_ff0069c6_16 (
    .in_2(and_12_out), .in_3(ful_adder_ff0069c6_14_out_4), .in_1(in_24), .out_5(ful_adder_ff0069c6_16_out_5),
    .out_4(ful_adder_ff0069c6_16_out_4));
  ful_adder_ff0069c6 ful_adder_ff0069c6_17 (
    .in_2(ful_adder_ff0069c6_15_out_4), .in_3(out_54), .in_1(ful_adder_ff0069c6_19_out_5),
    .out_5(ful_adder_ff0069c6_17_out_5), .out_4(out_62));
  and and_13 (and_13_out, 1'b1, A_out);
  and and_14 (and_14_out, B_out, 1'b0);
  ful_adder_ff0069c6 ful_adder_ff0069c6_18 (
    .in_2(and_14_out), .in_3(and_13_out), .in_1(in_22), .out_5(ful_adder_ff0069c6_18_out_5),
    .out_4(ful_adder_ff0069c6_18_out_4));
  and and_15 (and_15_out, 1'b0, C_out);
  ful_adder_ff0069c6 ful_adder_ff0069c6_19 (
    .in_2(out_55), .in_3(ful_adder_ff0069c6_18_out_4), .in_1(ful_adder_ff0069c6_20_out_5),
    .out_5(ful_adder_ff0069c6_19_out_5), .out_4(out_63));
  and and_16 (and_16_out, A_out, 1'b0);
  ful_adder_ff0069c6 ful_adder_ff0069c6_20 (
    .in_2(or_4_out), .in_3(and_16_out), .in_1(in_26), .out_5(ful_adder_ff0069c6_20_out_5), .out_4(LSB));
  not not_1 (not_1_out, in_37);
  not not_2 (not_2_out, in_38);
  not not_3 (not_3_out, in_39);
  Comparator comparator_1 (.a(in_27), .b(in_28), .gt(out_65), .eq(comparator_1_eq), .lt(comparator_1_lt));
  Subtractor subtractor_1 (.a(in_27), .b(in_28), .out(out_66));  // open: bin, bout
  not not_4 (not_4_out, in_40);
  or or_1 (out_53, in_20, in_19);
  or or_2 (out_54, in_18, in_17, in_16, in_15);
  or or_3 (out_55, in_18, in_17, in_14, in_13);
  or or_4 (or_4_out, in_12, in_14, in_16, in_18, in_20);
  Multiplier multiplier_1 (.a(out_66), .b(in_30), .out(multiplier_1_out));  // open: cin, cout
  Adder adder_1 (.a(multiplier_1_out), .b(in_29), .out(out_67));  // open: cin, cout
  Hex_Digit_Display hex_digit_display_1 (.value(in_36));  // open: dp
  Divider divider_1 (.a(out_67), .b(in_31), .out(out_69), .rem(out_70));  // open: upper
  and D0_0 (out_73, not_1_out, not_2_out, not_3_out, not_4_out);
  and D1_0 (out_77, not_1_out, not_2_out, not_3_out, in_40);
  and D2_0 (out_81, not_2_out, in_39, not_4_out);
  and D3_0 (out_85, not_2_out, in_39, in_40);
  and D4_0 (out_89, in_38, not_3_out, not_4_out);
  and D5_0 (out_93, in_38, not_3_out, in_40);
  and D6_0 (out_97, in_38, in_39, not_4_out);
  and D7_0 (out_101, in_38, in_39, in_40);
  and D8_0 (out_105, in_37, not_4_out);
  and D9_0 (out_109, in_37, in_40);
  or or_5 (out_68, comparator_1_eq, comparator_1_lt);
  not not_5 (not_5_out, in_41);
  not not_6 (not_6_out, in_42);
  not not_7 (not_7_out, in_43);
  not not_8 (not_8_out, in_44);
  and D0 (out_74, not_5_out, not_6_out, not_7_out, not_8_out);
  and D1 (out_78, not_5_out, not_6_out, not_7_out, in_44);
  and D2 (out_82, not_6_out, in_43, not_8_out);
  and D3 (out_86, not_6_out, in_43, in_44);
  and D4 (out_90, in_42, not_7_out, not_8_out);
  and D5 (out_94, in_42, not_7_out, in_44);
  and D6 (out_98, in_42, in_43, not_8_out);
  and D7 (out_102, in_42, in_43, in_44);
  and D8 (out_106, in_41, not_8_out);
  and D9 (out_110, in_41, in_44);
  Hex_Digit_Display hex_digit_display_2 (.value(in_35), .dp(undriven));
  not not_9 (not_9_out, in_49);
  Divider divider_2 (.a(in_29), .b(in_32), .out(out_71), .rem(out_72));  // open: upper
  not not_10 (not_10_out, in_50);
  not not_11 (not_11_out, in_51);
  not not_12 (not_12_out, in_52);
  and and_17 (out_76, not_9_out, not_10_out, not_11_out, not_12_out);
  and and_18 (out_80, not_9_out, not_10_out, not_11_out, in_52);
  and and_19 (out_84, not_10_out, in_51, not_12_out);
  and and_20 (out_88, not_10_out, in_51, in_52);
  and and_21 (out_92, in_50, not_11_out, not_12_out);
  and and_22 (out_96, in_50, not_11_out, in_52);
  and and_23 (out_100, in_50, in_51, not_12_out);
  and and_24 (out_104, in_50, in_51, in_52);
  and and_25 (out_108, in_49, not_12_out);
  and and_26 (out_112, in_49, in_52);
  Hex_Digit_Display hex_digit_display_3 (.value(in_34));  // open: dp
  not not_13 (not_13_out, in_45);
  not not_14 (not_14_out, w);
  not not_15 (not_15_out, x);
  not not_16 (not_16_out, y);
  and and_27 (out_75, not_13_out, not_14_out, not_15_out, not_16_out);
  and and_28 (out_79, not_13_out, not_14_out, not_15_out, y);
  and and_29 (out_83, not_14_out, x, not_16_out);
  and and_30 (out_87, not_14_out, x, y);
  and and_31 (out_91, w, not_15_out, not_16_out);
  and and_32 (out_95, w, not_15_out, y);
  and and_33 (out_99, w, x, not_16_out);
  and and_34 (out_103, w, x, y);
  and and_35 (out_107, in_45, not_16_out);
  and and_36 (out_111, in_45, y);
  Hex_Digit_Display hex_digit_display_4 (.value(in_33));  // open: dp

  // Notes on the sheet:
  //   MSB
  //   TIME
  //   0
  //   MSB
  //   Fixed at 60
  //   Set p value
  //   Set q value 
  //   Ticket price rates
  //   Let p = 30Rs
  //   Let q=2 Rs
  //   9
  //   w
  //   x
  //   y
  //   LSB
  //   Fixed at 10
  //   z
  //   0
  //   9
  //   Circuit called if T>60
  //   w
  //   x
  //   y
  //   z
  //   0
  //   9
  //   w
  //   x
  //   y
  //   z
  //   0
  //   Circuit called if T<60
  //   9
  //   z
  //   0
  //   9
endmodule

module ful_adder_ff0069c6 (
  input  in_1,
  input  in_2,
  input  in_3,
  output out_4,
  output out_5
);

  Adder #(.width(1)) adder_1 (.a(in_2), .b(in_3), .out(out_4), .cin(in_1), .cout(out_5));
endmodule
